# Fritzing sketch data-logger-circuit (saved by Fritzing 0.9.4)
circuit board: 8.46667cm x 5.64444cm
breadboards: 1

parts:
  Part1 = Arduino Nano (Rev3.0)
  microSD1 = MicroSD Card Module
  R1 = Resistor [tolerance=±5% resistance=330 package="0603 [SMD]"]
  User_indicator = LED - 3mm [color="Green (570nm)" package="3 mm [THT]"]
  Temperature_sensor = DS18B20 1-Wire Temperature Sensor [part_number=DS18B20]

nets:
  N1: Part1.D2, R1.Pin_0
  N2: Part1.D3, Temperature_sensor.DQ
  N3: Part1.D10, microSD1.CS
  N4: Part1.D11/MOSI, microSD1.MOSI
  N5: Part1.D12/MISO, microSD1.MISO
  5V: Part1.5V, microSD1.VCC, Temperature_sensor.VDD
  N6: Part1.D13/SCK, microSD1.SCK
  GND: microSD1.GND, User_indicator.cathode, Temperature_sensor.GND
  N7: R1.Pin_1, User_indicator.anode
