# Fritzing sketch data-logger-v2 (saved by Fritzing 0.9.4)
breadboards: 1

parts:
  Part2 = Arduino Nano (Rev3.0)
  S1 = Pushbutton [package="[THT]"]
  Grove1 = Grove OLED 128x96
  ZS-042_RTC1 = ZS-042 RTC Module
  microSD2 = MicroSD Card Module
  C1 = Electrolytic Capacitor [capacitance=100nF package="100 mil [THT, electrolytic]"]

nets:
  GND: Part2.GND, S1.Pin_1, S1.Pin_2, ZS-042_RTC1.GND#0, microSD2.GND, C1.-
  N1: Part2.D2, S1.Pin_3, S1.Pin_4, C1.+
  N2: Part2.D3, ZS-042_RTC1.SQW
  N3: Part2.D4, ZS-042_RTC1.SDA#2
  N4: Part2.D5, ZS-042_RTC1.SCL#3
  N5: Part2.D10, microSD2.CS
  N6: Part2.D11/MOSI, microSD2.MOSI
  N7: Part2.D12/MISO, microSD2.MISO
  5V: Part2.5V, ZS-042_RTC1.VCC#1, microSD2.VCC
  N8: Part2.D13/SCK, microSD2.SCK
  N9: Grove1.GND, ZS-042_RTC1.GND#6
  N10: Grove1.VCC, ZS-042_RTC1.VCC#7
  N11: Grove1.SDA, ZS-042_RTC1.SDA#8
  N12: Grove1.SCL, ZS-042_RTC1.SCL#9
